# Fritzing sketch Slot_Machine (saved by Fritzing 0.9.3b)
breadboards: 1

parts:
  Arduino_Uno_(Rev3) = Arduino Uno (Rev3)
  Motor_(Reel2) = Stepper Motor - Bipolar
  Motor_(Reel3) = Stepper Motor - Bipolar
  Servo_(Pull-Arm) = Basic Servo
  Buzzer = LilyPad Buzzer
  Photocell_(LDR) = Photocell (LDR) [package=THT]
  10k_Resistor = Resistor [tolerance=±5% resistance=220 package=THT]
  Arduino_CNC_Shield_V3_00_1 = Arduino_CNC_V3.00
  Q1 = NPN-Transistor [package="SOT-23 [SMD]"]
  R1 = Resistor [tolerance=±5% resistance=100 package=THT]
  LED1 = RGB LED (com. cathode, rbg) [package="5 mm [THT]"]
  R2 = Resistor [tolerance=±5% resistance=220 package="0603 [SMD]"]
  R3 = Resistor [tolerance=±5% resistance=220 package="0603 [SMD]"]
  R4 = Resistor [tolerance=±5% resistance=220 package="0603 [SMD]"]
  Arduino_Uno_(Rev3)1 = Arduino Uno (Rev3)
  Motor_(Reel2)1 = Stepper Motor - Bipolar
  Part1 = Thumb Joystick

nets:
  N1: Arduino_Uno_(Rev3).A0, Part1.VERT
  N2: Arduino_Uno_(Rev3).A1, Part1.HORZ
  N3: Arduino_Uno_(Rev3).D9_PWM, Servo_(Pull-Arm).pulse
  N4: Arduino_Uno_(Rev3).D10_PWM/SS, 10k_Resistor.Pin_1
  GND: Arduino_Uno_(Rev3).GND, Servo_(Pull-Arm).gnd, Photocell_(LDR).pin_1, Q1.2, R1.Pin_0, R1.Pin_1, Arduino_Uno_(Rev3)1.GND, Part1.GND
  N5: Arduino_Uno_(Rev3).D0/RX, Arduino_Uno_(Rev3)1.D1/TX
  N6: Arduino_Uno_(Rev3).D1/TX, Arduino_Uno_(Rev3)1.D0/RX
  N7: Arduino_Uno_(Rev3).D3_PWM, LED1.green_anode, R4.Pin_1
  N8: Arduino_Uno_(Rev3).D5_PWM, LED1.blue_anode, R3.Pin_1
  N9: Arduino_Uno_(Rev3).D6_PWM, LED1.red_anode, R2.Pin_0, R2.Pin_1
  VCC: Arduino_Uno_(Rev3).5V, Servo_(Pull-Arm).vcc, Buzzer.-, Photocell_(LDR).pin_0, LED1.common_cathode, Part1.VCC
  N10: Motor_(Reel2).A, Arduino_CNC_Shield_V3_00_1.X-MTR_'1'
  N11: Motor_(Reel2).C, Arduino_CNC_Shield_V3_00_1.X-MTR_'2'
  N12: Motor_(Reel2).B, Arduino_CNC_Shield_V3_00_1.X-MTR_'3'
  N13: Motor_(Reel2).D, Arduino_CNC_Shield_V3_00_1.X-MTR_'4'
  N14: Motor_(Reel3).A, Arduino_CNC_Shield_V3_00_1.Z-MTR_'1'
  N15: Motor_(Reel3).C, Arduino_CNC_Shield_V3_00_1.Z-MTR_'2'
  N16: Motor_(Reel3).B, Arduino_CNC_Shield_V3_00_1.Z-MTR_'3'
  N17: Motor_(Reel3).D, Arduino_CNC_Shield_V3_00_1.Z-MTR_'4'
  N18: Buzzer.+, Q1.1
  N19: 10k_Resistor.Pin_0, Q1.0
  N20: Arduino_CNC_Shield_V3_00_1.Y-MTR_'1', Motor_(Reel2)1.A
  N21: Arduino_CNC_Shield_V3_00_1.Y-MTR_'2', Motor_(Reel2)1.C
  N22: Arduino_CNC_Shield_V3_00_1.Y-MTR_'3', Motor_(Reel2)1.B
  N23: Arduino_CNC_Shield_V3_00_1.Y-MTR_'4', Motor_(Reel2)1.D
  N24: Arduino_CNC_Shield_V3_00_1.A_-_M0_(5V), Arduino_Uno_(Rev3)1.A0
  N25: Arduino_CNC_Shield_V3_00_1.A_-_M1_(5V), Arduino_Uno_(Rev3)1.A1
  N26: Arduino_CNC_Shield_V3_00_1.A_-_M2_(5V), Arduino_Uno_(Rev3)1.A2

notes:
  The CNC shield would be connected on top of the Arduino to the left
  Made by: George Sun

custom parts:
  Arduino_CNC_V3.00: Protoneer Arduino CNC Shield V3.00 If using Grbl V0.9: The “A” axis can not be used (yet). The “SCL” (Arduino A5) pin is now used for 'Probing' input. The “End Stops Z+ & Z-” (Arduino D11) and “SpnEn” (Arduino D12) have been switched!
